# Fritzing sketch cistercian (saved by Fritzing 0.9.3b)
circuit board: 3.3cm x 3.302cm
breadboards: 1

parts:
  J1 = female pin header, 12 pins [form="♀ (female)"]
  J2 = female pin header, 12 pins [form="♀ (female)"]
  LED1 = smd LED [color="Red (633nm)" package="0603 [SMD]"]
  LED2 = smd LED [color="Red (633nm)" package="0603 [SMD]"]
  LED3 = smd LED [color="Red (633nm)" package="0603 [SMD]"]
  LED4 = smd LED [color="Red (633nm)" package="0603 [SMD]"]
  LED5 = smd LED [color="Red (633nm)" package="0603 [SMD]"]
  LED6 = smd LED [color="Red (633nm)" package="0603 [SMD]"]
  LED7 = smd LED [color="Red (633nm)" package="0603 [SMD]"]
  LED8 = smd LED [color="Red (633nm)" package="0603 [SMD]"]
  LED9 = smd LED [color="Red (633nm)" package="0603 [SMD]"]
  LED10 = smd LED [color="Red (633nm)" package="0603 [SMD]"]
  LED11 = smd LED [color="Red (633nm)" package="0603 [SMD]"]
  LED12 = smd LED [color="Red (633nm)" package="0603 [SMD]"]
  LED13 = smd LED [color="Red (633nm)" package="0603 [SMD]"]
  LED14 = smd LED [color="Red (633nm)" package="0603 [SMD]"]
  LED15 = smd LED [color="Red (633nm)" package="0603 [SMD]"]
  LED16 = smd LED [color="Red (633nm)" package="0603 [SMD]"]
  LED17 = smd LED [color="Red (633nm)" package="0603 [SMD]"]
  LED18 = smd LED [color="Red (633nm)" package="0603 [SMD]"]
  LED19 = smd LED [color="Red (633nm)" package="0603 [SMD]"]
  LED20 = smd LED [color="Red (633nm)" package="0603 [SMD]"]
  LED21 = smd LED [color="Red (633nm)" package="0603 [SMD]"]
  LED22 = smd LED [color="Red (633nm)" package="0603 [SMD]"]
  LED23 = smd LED [color="Red (633nm)" package="0603 [SMD]"]
  LED24 = smd LED [color="Red (633nm)" package="0603 [SMD]"]
  LED25 = smd LED [color="Red (633nm)" package="0603 [SMD]"]
  LED26 = smd LED [color="Red (633nm)" package="0603 [SMD]"]
  LED27 = smd LED [color="Red (633nm)" package="0603 [SMD]"]
  LED28 = smd LED [color="Red (633nm)" package="0603 [SMD]"]
  LED29 = smd LED [color="Red (633nm)" package="0603 [SMD]"]
  LED30 = smd LED [color="Red (633nm)" package="0603 [SMD]"]
  LED31 = smd LED [color="Red (633nm)" package="0603 [SMD]"]
  LED32 = smd LED [color="Red (633nm)" package="0603 [SMD]"]
  LED33 = smd LED [color="Red (633nm)" package="0603 [SMD]"]
  LED34 = smd LED [color="Red (633nm)" package="0603 [SMD]"]
  LED35 = smd LED [color="Red (633nm)" package="0603 [SMD]"]
  LED36 = smd LED [color="Red (633nm)" package="0603 [SMD]"]
  LED37 = smd LED [color="Red (633nm)" package="0603 [SMD]"]
  LED38 = smd LED [color="Red (633nm)" package="0603 [SMD]"]
  LED39 = smd LED [color="Red (633nm)" package="0603 [SMD]"]
  LED40 = smd LED [color="Red (633nm)" package="0603 [SMD]"]
  LED41 = smd LED [color="Red (633nm)" package="0603 [SMD]"]
  LED42 = smd LED [color="Red (633nm)" package="0603 [SMD]"]
  LED43 = smd LED [color="Red (633nm)" package="0603 [SMD]"]
  LED44 = smd LED [color="Red (633nm)" package="0603 [SMD]"]
  LED45 = smd LED [color="Red (633nm)" package="0603 [SMD]"]
  LED46 = smd LED [color="Red (633nm)" package="0603 [SMD]"]

nets:
  N1: J1.pin1, LED12.anode
  N2: J1.pin2, LED2.anode
  N3: J1.pin3, LED5.anode
  N4: J1.pin4, LED4.anode
  N5: J1.pin5, LED10.anode
  N6: J1.pin6, LED46.anode
  N7: J1.pin7, LED30.anode
  N8: J1.pin8, LED35.anode
  N9: J1.pin9, LED29.anode
  N10: J1.pin10, LED44.anode
  N11: J1.pin11, LED34.anode
  N12: J1.pin12, LED1.cathode, LED3.cathode, LED7.cathode, LED8.cathode, LED9.cathode, LED11.cathode, LED16.cathode, LED18.cathode, LED19.cathode, LED21.cathode, LED22.cathode, LED23.cathode, LED26.cathode, LED27.cathode, LED28.cathode, LED33.cathode, LED36.cathode, LED37.cathode, LED38.cathode, LED39.cathode, LED42.cathode, LED43.cathode, LED45.cathode
  N13: J2.pin1, LED6.anode
  N14: J2.pin2, LED17.anode
  N15: J2.pin3, LED13.anode
  N16: J2.pin4, LED14.anode
  N17: J2.pin5, LED20.anode
  N18: J2.pin6, LED15.anode
  N19: J2.pin7, LED31.anode
  N20: J2.pin8, LED24.anode
  N21: J2.pin9, LED25.anode
  N22: J2.pin10, LED32.anode
  N23: J2.pin11, LED41.anode
  N24: J2.pin12, LED40.anode
  N25: LED1.anode, LED2.cathode
  N26: LED3.anode, LED4.cathode
  N27: LED5.cathode, LED8.anode
  N28: LED6.cathode, LED7.anode
  N29: LED9.anode, LED10.cathode
  N30: LED11.anode, LED12.cathode
  N31: LED13.cathode, LED22.anode
  N32: LED14.cathode, LED21.anode
  N33: LED15.cathode, LED18.anode
  N34: LED16.anode, LED20.cathode
  N35: LED17.cathode, LED19.anode
  N36: LED23.anode, LED31.cathode
  N37: LED24.cathode, LED42.anode
  N38: LED25.cathode, LED43.anode
  N39: LED26.anode, LED41.cathode
  N40: LED27.anode, LED29.cathode
  N41: LED28.anode, LED34.cathode
  N42: LED30.cathode, LED38.anode
  N43: LED32.cathode, LED37.anode
  N44: LED33.anode, LED44.cathode
  N45: LED35.cathode, LED39.anode
  N46: LED36.anode, LED40.cathode
  N47: LED45.anode, LED46.cathode

notes:
  GND
  CTR
  1
  6
  2
  3
  4
  Cistercian Numeric Display
  www.kreativekorp.com
