# Fritzing sketch kaktovik (saved by Fritzing 0.9.3b)
circuit board: 2.51cm x 2.12cm
breadboards: 1

parts:
  LED1 = smd LED [color="Red (633nm)" package="0603 [SMD]"]
  LED2 = smd LED [color="Red (633nm)" package="0603 [SMD]"]
  LED3 = smd LED [color="Red (633nm)" package="0603 [SMD]"]
  LED4 = smd LED [color="Red (633nm)" package="0603 [SMD]"]
  LED5 = smd LED [color="Red (633nm)" package="0603 [SMD]"]
  LED6 = smd LED [color="Red (633nm)" package="0603 [SMD]"]
  LED7 = smd LED [color="Red (633nm)" package="0603 [SMD]"]
  LED8 = smd LED [color="Red (633nm)" package="0603 [SMD]"]
  LED9 = smd LED [color="Red (633nm)" package="0603 [SMD]"]
  LED10 = smd LED [color="Red (633nm)" package="0603 [SMD]"]
  LED11 = smd LED [color="Red (633nm)" package="0603 [SMD]"]
  LED12 = smd LED [color="Red (633nm)" package="0603 [SMD]"]
  LED13 = smd LED [color="Red (633nm)" package="0603 [SMD]"]
  LED14 = smd LED [color="Red (633nm)" package="0603 [SMD]"]
  LED15 = smd LED [color="Red (633nm)" package="0603 [SMD]"]
  LED16 = smd LED [color="Red (633nm)" package="0603 [SMD]"]
  LED17 = smd LED [color="Red (633nm)" package="0603 [SMD]"]
  LED18 = smd LED [color="Red (633nm)" package="0603 [SMD]"]
  J1 = female pin header, 9 pins [form="♀ (female)"]
  J2 = female pin header, 9 pins [form="♀ (female)"]

nets:
  N1: LED1.cathode, LED2.cathode, LED3.cathode, LED4.cathode, LED5.cathode, LED6.cathode, LED7.cathode, LED8.cathode, LED9.cathode, J2.pin7
  N2: LED1.anode, LED18.anode, J2.pin3
  N3: LED2.anode, LED14.anode, J2.pin1
  N4: LED3.anode, LED11.anode, J1.pin7
  N5: LED4.anode, LED17.anode, J1.pin1
  N6: LED5.anode, LED16.anode, J1.pin9
  N7: LED6.anode, LED10.anode, J2.pin9
  N8: LED7.anode, LED13.anode, J2.pin4
  N9: LED8.anode, LED12.anode, J1.pin6
  N10: LED9.anode, LED15.anode, J1.pin8
  N11: LED10.cathode, LED11.cathode, LED12.cathode, LED13.cathode, LED14.cathode, LED15.cathode, LED16.cathode, LED17.cathode, LED18.cathode, J2.pin2

notes:
  Dual Kaktovik Numeric Display
  www.kreativekorp.com
  #2 COM2 #1  10  NC  NC COM1 NC  #5
  CP  DP  #3  15  NC  NC  NC  NC  #4
