# Fritzing sketch buck (saved by Fritzing 0.9.3b)
circuit board: 10.1776cm x 5.36194cm
circuit board: 2.55cm x 3.5cm
circuit board: 24.1cm x 5.33cm
circuit board: 5cm x 2.7cm
circuit board: 2.1cm x 3.2cm
circuit board: 5cm x 2.7cm
circuit board: 5cm x 2.7cm
circuit board: 5cm x 2.7cm
circuit board: 3.3cm x 3.302cm
breadboards: 1

parts:
  J10 = female pin header, 5 pins [form="♀ (female)"]
  J11 = female pin header, 5 pins [form="♀ (female)"]
  J12 = female pin header, 5 pins [form="♀ (female)"]
  J13 = female pin header, 5 pins [form="♀ (female)"]
  J1 = female pin header, 10 pins [form="♀ (female)"]
  J2 = female pin header, 8 pins [form="♀ (female)"]  # not connected
  J3 = female pin header, 8 pins [form="♀ (female)"]
  J7 = female pin header, 8 pins [form="♀ (female)"]
  J6 = female pin header, 8 pins [form="♀ (female)"]
  J5 = female pin header, 8 pins [form="♀ (female)"]
  SW8 = Pushbutton [package="[THT]"]
  SW7 = Pushbutton [package="[THT]"]
  SW6 = Pushbutton [package="[THT]"]
  SW5 = Pushbutton [package="[THT]"]
  SW4 = Pushbutton [package="[THT]"]
  SW3 = Pushbutton [package="[THT]"]
  SW2 = Pushbutton [package="[THT]"]
  SW1 = Pushbutton [package="[THT]"]
  J4 = double row female pin header, 36 pins [form="♀ (female)"]
  J9 = female pin header, 12 pins [form="♀ (female)"]
  IC2 = IC, DIP package, 24 pins [chip_label=IC]
  J8 = female pin header, 12 pins [form="♀ (female)"]
  D1 = LED - 5mm [color="Red (633nm)" package="5 mm [THT]"]
  IC1 = IC, DIP package, 24 pins [chip_label=IC]
  PCB2 = Arduino Mega Shield PCB  # not connected
  SW9 = Pushbutton [package="[THT]"]
  PIEZO = female pin header, 2 pins [form="♀ (female)"]
  R27 = PHOTOCELL [package=photocell]
  R26 = Resistor [tolerance=±5% resistance=1k package=THT]
  RPIEZO = Resistor [tolerance=±5% resistance=220 package=THT]
  J14 = female pin header, 9 pins [form="♀ (female)"]
  J15 = female pin header, 8 pins [form="♀ (female)"]
  J16 = female pin header, 5 pins [form="♀ (female)"]

nets:
  N1: J10.pin1, J10.pin2, J11.pin1, J11.pin2, J12.pin1, J12.pin2, J13.pin1, J13.pin2, J7.pin5, J4.pin1, J4.pin36, R27.P$1, J14.pin8, J15.pin5, J16.pin5
  N2: J10.pin3, J11.pin3, J12.pin3, J13.pin3, J1.pin4, J7.pin6, J7.pin7, SW8.Pin_3, SW8.Pin_4, SW7.Pin_3, SW7.Pin_4, SW6.Pin_3, SW6.Pin_4, SW5.Pin_3, SW5.Pin_4, SW4.Pin_3, SW4.Pin_4, SW3.Pin_3, SW3.Pin_4, SW2.Pin_3, SW2.Pin_4, SW1.Pin_3, SW1.Pin_4, J4.pin18, J4.pin19, J8.pin12, D1.cathode, SW9.Pin_1, SW9.Pin_2, PIEZO.pin1, R26.Pin_1, J14.pin7, J15.pin2, J15.pin7, J16.pin4
  N3: J10.pin4, J11.pin4, J12.pin4, J13.pin4, J1.pin2, J3.pin7, J16.pin1
  N4: J10.pin5, J11.pin5, J12.pin5, J13.pin5, J1.pin1, J3.pin8, J16.pin2
  N5: J1.pin10, RPIEZO.Pin_1
  N6: J3.pin1, J14.pin6
  N7: J3.pin2, J14.pin5
  N8: J3.pin3, J15.pin4
  N9: J3.pin4, J15.pin3
  N10: J3.pin5, J14.pin9, J16.pin3
  N11: J3.pin6, J14.pin4
  N12: J7.pin3, SW9.Pin_3, SW9.Pin_4
  N13: J6.pin1, SW8.Pin_1, SW8.Pin_2
  N14: J6.pin2, SW7.Pin_1, SW7.Pin_2
  N15: J6.pin3, SW6.Pin_1
  N16: J6.pin4, SW5.Pin_1
  N17: J6.pin5, SW4.Pin_1, SW4.Pin_2
  N18: J6.pin6, SW3.Pin_1, SW3.Pin_2
  N19: J6.pin7, SW2.Pin_1, SW2.Pin_2
  N20: J6.pin8, SW1.Pin_1, SW1.Pin_2
  N21: J5.pin1, R27.P$2, R26.Pin_0
  N22: J4.pin2, IC2.pin13
  N23: J4.pin3, IC2.pin14
  N24: J4.pin4, IC2.pin15
  N25: J4.pin5, IC2.pin16
  N26: J4.pin6, IC2.pin17
  N27: J4.pin7, IC2.pin18
  N28: J4.pin8, IC2.pin19
  N29: J4.pin9, IC2.pin20
  N30: J4.pin10, IC2.pin21
  N31: J4.pin11, IC2.pin22
  N32: J4.pin12, IC2.pin23
  N33: J4.pin13, IC2.pin24
  N34: J4.pin24, IC1.pin24
  N35: J4.pin25, IC1.pin23
  N36: J4.pin26, IC1.pin22
  N37: J4.pin27, IC1.pin21
  N38: J4.pin28, IC1.pin20
  N39: J4.pin29, IC1.pin19
  N40: J4.pin30, IC1.pin18
  N41: J4.pin31, IC1.pin17
  N42: J4.pin32, IC1.pin16
  N43: J4.pin33, IC1.pin15
  N44: J4.pin34, IC1.pin14
  N45: J4.pin35, IC1.pin13
  N46: J9.pin1, IC2.pin1
  N47: J9.pin2, IC2.pin2
  N48: J9.pin3, IC2.pin3
  N49: J9.pin4, IC2.pin4
  N50: J9.pin5, IC2.pin5
  N51: J9.pin6, IC2.pin6
  N52: J9.pin7, IC2.pin7
  N53: J9.pin8, IC2.pin8
  N54: J9.pin9, IC2.pin9
  N55: J9.pin10, IC2.pin10
  N56: J9.pin11, IC2.pin11
  N57: J9.pin12, IC2.pin12
  N58: J8.pin1, IC1.pin1
  N59: J8.pin2, IC1.pin2
  N60: J8.pin3, IC1.pin3
  N61: J8.pin4, IC1.pin4
  N62: J8.pin5, IC1.pin5
  N63: J8.pin6, IC1.pin6
  N64: J8.pin7, IC1.pin7
  N65: J8.pin8, IC1.pin8
  N66: J8.pin9, IC1.pin9
  N67: J8.pin10, IC1.pin10
  N68: J8.pin11, IC1.pin11
  N69: D1.anode, IC1.pin12
  N70: PIEZO.pin2, RPIEZO.Pin_0

notes:
  6
  4
  1
  3
  2
  CTR
  GND
  + + - D C
  RESET
  F1    F2    F3    F4    F5    F6    F7    F8
  1K
  -[50]-
  -[220]-
  PS VI GD RX TX FX VB EN 3V
  ALARM
  Beckie's Ultimate Clock Kit
  www.kreativekorp.com
  FU GD RS VI RX TX CS MD
  5V GD SW CL DA
  R1
  R2
  R3
  R4
  R5
  R6
  R7
  R8
  R9
  R10
  R11
  R12
  R24
  R23
  R22
  R21
  R20
  R19
  R15
  R17
  R13
  R16
  R18
  R14
  R25
  R26
  R27
  J1
  J2
  J3
  J4
  J5
  J6
  J7
  GPS
  Bluetooth
  RTC

custom parts:
  Arduino Mega Shield PCB: Plain PCB Shaped to fit an Arduino Mega R3 "Shield"
